// Digital circuit 16bit_eq.dig as structural Verilog
module _16bit_eq (
  input  [15:0] a,
  input  [15:0] b,
  output r
);

  wire _8bit_eq_1_r, _8bit_eq_2_r;

  _8bit_eq _8bit_eq_1 (.a(a[7:0]), .b(b[7:0]), .r(_8bit_eq_1_r));
  _8bit_eq _8bit_eq_2 (.a(a[15:8]), .b(b[15:8]), .r(_8bit_eq_2_r));
  and and_1 (r, _8bit_eq_1_r, _8bit_eq_2_r);
endmodule
