// Digital circuit 2bit_eq.dig as structural Verilog
module _2bit_eq (
  input  [1:0] a,
  input  [1:0] b,
  output r
);

  wire xnor_1_out, xnor_2_out;

  xnor xnor_1 (xnor_1_out, a[0], b[0]);
  xnor xnor_2 (xnor_2_out, a[1], b[1]);
  and and_1 (r, xnor_1_out, xnor_2_out);
endmodule
