// Digital circuit 32bit_eq.dig as structural Verilog
module _32bit_eq (
  input  [31:0] a,
  input  [31:0] b,
  output r
);

  wire _16bit_eq_1_r, _16bit_eq_2_r;

  _16bit_eq _16bit_eq_1 (.a(a[15:0]), .b(b[15:0]), .r(_16bit_eq_1_r));
  _16bit_eq _16bit_eq_2 (.a(a[31:16]), .b(b[31:16]), .r(_16bit_eq_2_r));
  and and_1 (r, _16bit_eq_1_r, _16bit_eq_2_r);
endmodule
