// Digital circuit 4bit_eq.dig as structural Verilog
module _4bit_eq (
  input  [3:0] a,
  input  [3:0] b,
  output r
);

  wire _2bit_eq_1_r, _2bit_eq_2_r;

  _2bit_eq _2bit_eq_1 (.a(a[1:0]), .b(b[1:0]), .r(_2bit_eq_1_r));
  _2bit_eq _2bit_eq_2 (.a(a[3:2]), .b(b[3:2]), .r(_2bit_eq_2_r));
  and and_1 (r, _2bit_eq_1_r, _2bit_eq_2_r);
endmodule
