// Digital circuit 8-bit-ripple-carry-adder.dig as structural Verilog
module _8_bit_ripple_carry_adder (
  input  [7:0] a,
  input  [7:0] b,
  input  [7:0] cin,
  output sum,
  output cout
);

  wire add_2_c_o, add_2_s, add_3_c_o, add_3_s, add_4_c_o, add_4_s, add_5_c_o, add_5_s, add_6_c_o, add_6_s,
       add_7_c_o, add_7_s, add_8_c_o, add_8_s;

  Add add_1 (.a(a[0]), .b(b[0]), .c_i(cin[0]), .s(sum), .c_o(cout));
  Add add_2 (.a(a[1]), .b(b[1]), .c_i(cin[1]), .s(add_2_s), .c_o(add_2_c_o));
  Add add_3 (.a(a[2]), .b(b[2]), .c_i(cin[2]), .s(add_3_s), .c_o(add_3_c_o));
  Add add_4 (.a(a[3]), .b(b[3]), .c_i(cin[3]), .s(add_4_s), .c_o(add_4_c_o));
  Add add_5 (.a(a[4]), .b(b[4]), .c_i(cin[4]), .s(add_5_s), .c_o(add_5_c_o));
  Add add_6 (.a(a[5]), .b(b[5]), .c_i(cin[5]), .s(add_6_s), .c_o(add_6_c_o));
  Add add_7 (.a(a[6]), .b(b[6]), .c_i(cin[6]), .s(add_7_s), .c_o(add_7_c_o));
  Add add_8 (.a(a[7]), .b(b[7]), .c_i(cin[7]), .s(add_8_s), .c_o(add_8_c_o));
endmodule
