// Digital circuit 8bit_adder.dig as structural Verilog
module _8bit_adder (
  input  [7:0] A,
  input  [7:0] B,
  output [7:0] sum
);

  wire _1_bit_full_adder_1_cout, _1_bit_full_adder_2_cout, _1_bit_full_adder_3_cout,
       _1_bit_full_adder_4_cout, _1_bit_full_adder_5_cout, _1_bit_full_adder_6_cout,
       _1_bit_full_adder_7_cout, _1_bit_full_adder_8_cout;

  _1_bit_full_adder _1_bit_full_adder_1 (.a(A[0]), .b(B[0]), .cin(1'b0), .sum(sum[0]), .cout(_1_bit_full_adder_1_cout));
  _1_bit_full_adder _1_bit_full_adder_2 (
    .a(A[1]), .b(B[1]), .cin(_1_bit_full_adder_1_cout), .sum(sum[1]), .cout(_1_bit_full_adder_2_cout));
  _1_bit_full_adder _1_bit_full_adder_3 (
    .a(A[2]), .b(B[2]), .cin(_1_bit_full_adder_2_cout), .sum(sum[2]), .cout(_1_bit_full_adder_3_cout));
  _1_bit_full_adder _1_bit_full_adder_4 (
    .a(A[3]), .b(B[3]), .cin(_1_bit_full_adder_3_cout), .sum(sum[3]), .cout(_1_bit_full_adder_4_cout));
  _1_bit_full_adder _1_bit_full_adder_5 (
    .a(A[4]), .b(B[4]), .cin(_1_bit_full_adder_4_cout), .sum(sum[4]), .cout(_1_bit_full_adder_5_cout));
  _1_bit_full_adder _1_bit_full_adder_6 (
    .a(A[5]), .b(B[5]), .cin(_1_bit_full_adder_5_cout), .sum(sum[5]), .cout(_1_bit_full_adder_6_cout));
  _1_bit_full_adder _1_bit_full_adder_7 (
    .a(A[6]), .b(B[6]), .cin(_1_bit_full_adder_6_cout), .sum(sum[6]), .cout(_1_bit_full_adder_7_cout));
  _1_bit_full_adder _1_bit_full_adder_8 (
    .a(A[7]), .b(B[7]), .cin(_1_bit_full_adder_7_cout), .sum(sum[7]), .cout(_1_bit_full_adder_8_cout));
  LED cout (.in(_1_bit_full_adder_8_cout));
endmodule
