// Digital circuit 8bit_counter.dig as structural Verilog
module _8bit_counter (
  input  CLK,
  input  CLR,
  output [7:0] COUNT
);

  wire [7:0] _8bit_adder_1_sum;

  _8bit_register_cir_en _8bit_register_cir_en_1 (.D(_8bit_adder_1_sum), .EN(1'b1), .CLR(CLR), .CLK(CLK), .Q(COUNT));
  _8bit_adder _8bit_adder_1 (.A(COUNT), .B(8'h1), .sum(_8bit_adder_1_sum));
endmodule
