// Digital circuit 8bit_eq.dig as structural Verilog
module _8bit_eq (
  input  [7:0] a,
  input  [7:0] b,
  output r
);

  wire _4bit_eq_1_r, _4bit_eq_2_r;

  _4bit_eq _4bit_eq_1 (.a(a[3:0]), .b(b[3:0]), .r(_4bit_eq_1_r));
  _4bit_eq _4bit_eq_2 (.a(a[7:4]), .b(b[7:4]), .r(_4bit_eq_2_r));
  and and_1 (r, _4bit_eq_1_r, _4bit_eq_2_r);
endmodule
