// Digital circuit 8bit_register_cir_en.dig as structural Verilog
module _8bit_register_cir_en (
  input  [7:0] D,
  input  EN,
  input  CLR,
  input  CLK,
  output [7:0] Q
);

  d_flipflop_cir d_flipflop_cir_1 (.D(D[0]), .CLK(CLK), .EN(EN), .CLR(CLR), .Q(Q[0]));  // open: NotQ
  d_flipflop_cir d_flipflop_cir_2 (.D(D[1]), .CLK(CLK), .EN(EN), .CLR(CLR), .Q(Q[1]));  // open: NotQ
  d_flipflop_cir d_flipflop_cir_3 (.D(D[2]), .CLK(CLK), .EN(EN), .CLR(CLR), .Q(Q[2]));  // open: NotQ
  d_flipflop_cir d_flipflop_cir_4 (.D(D[3]), .CLK(CLK), .EN(EN), .CLR(CLR), .Q(Q[3]));  // open: NotQ
  d_flipflop_cir d_flipflop_cir_5 (.D(D[4]), .CLK(CLK), .EN(EN), .CLR(CLR), .Q(Q[4]));  // open: NotQ
  d_flipflop_cir d_flipflop_cir_6 (.D(D[5]), .CLK(CLK), .EN(EN), .CLR(CLR), .Q(Q[5]));  // open: NotQ
  d_flipflop_cir d_flipflop_cir_7 (.D(D[6]), .CLK(CLK), .EN(EN), .CLR(CLR), .Q(Q[6]));  // open: NotQ
  d_flipflop_cir d_flipflop_cir_8 (.D(D[7]), .CLK(CLK), .EN(EN), .CLR(CLR), .Q(Q[7]));  // open: NotQ
endmodule
