// Digital circuit analyze_decode.dig as structural Verilog
module analyze_decode (
  input  [31:0] iw,
  output [2:0] itype
);

  wire _2bit_eq_1_r, _2bit_eq_2_r, _4bit_eq_1_r, _32bit_eq_1_r, _32bit_eq_2_r, _32bit_eq_3_r, _32bit_eq_4_r,
       and_1_out, and_2_out, and_3_out, and_4_out, comparator_1_eq, comparator_2_eq;

  _2bit_eq _2bit_eq_1 (.a(iw[27:26]), .b(2'b00), .r(_2bit_eq_1_r));
  _32bit_eq _32bit_eq_1 (.a({{26{1'b0}}, iw[27:22]}), .b({32{1'b0}}), .r(_32bit_eq_1_r));
  _32bit_eq _32bit_eq_2 (.a({{28{1'b0}}, iw[7:4]}), .b(32'h9), .r(_32bit_eq_2_r));
  _32bit_eq _32bit_eq_3 (.a({{8{1'b0}}, iw[27:4]}), .b(32'h12fff1), .r(_32bit_eq_3_r));
  _2bit_eq _2bit_eq_2 (.a(iw[27:26]), .b(2'b01), .r(_2bit_eq_2_r));
  Comparator comparator_1 (.a(iw[24]), .b(1'b1), .eq(comparator_1_eq));  // open: gt, lt
  Comparator comparator_2 (.a(iw[24]), .b(1'b0), .eq(comparator_2_eq));  // open: gt, lt
  _32bit_eq _32bit_eq_4 (.a({{29{1'b0}}, iw[27:25]}), .b(32'h5), .r(_32bit_eq_4_r));
  _4bit_eq _4bit_eq_1 (.a(iw[31:28]), .b(4'b1110), .r(_4bit_eq_1_r));
  and and_1 (and_1_out, _32bit_eq_1_r, _32bit_eq_2_r);
  and and_2 (and_2_out, comparator_1_eq, _32bit_eq_4_r);
  and and_3 (and_3_out, comparator_2_eq, _32bit_eq_4_r);
  and and_4 (and_4_out, _32bit_eq_4_r, ~_4bit_eq_1_r);  // And
  PriorityEncoder #(.Selector_Bits(3)) priorityencoder_1 (
    .in0(1'b0), .in1(_2bit_eq_1_r), .in2(_2bit_eq_2_r), .in3(and_3_out), .in4(and_2_out), .in5(and_4_out),
    .in6(and_1_out), .in7(_32bit_eq_3_r), .num(itype));  // open: any
endmodule
