// Digital circuit d_flipflop_cir.dig as structural Verilog
module d_flipflop_cir (
  input  D,
  input  CLK,
  input  EN,
  input  CLR,
  output Q,
  output NotQ
);

  wire d_latch_cir_1_q, multiplexer_1_out, not_1_out;

  Multiplexer multiplexer_1 (.sel(EN), .in_0(Q), .in_1(D), .out(multiplexer_1_out));
  not not_1 (not_1_out, CLK);
  d_latch_cir d_latch_cir_1 (.CLK(not_1_out), .D(multiplexer_1_out), .CLR(CLR), .Q(d_latch_cir_1_q));  // open: NotQ
  d_latch_cir d_latch_cir_2 (.CLK(CLK), .D(d_latch_cir_1_q), .CLR(CLR), .Q(Q), .NotQ(NotQ));
endmodule
