// Digital circuit fulladder.dig as structural Verilog
module fulladder (
  input  CI,
  input  A,
  input  B,
  output S,
  output CO
);

  wire halfadder_1_c, halfadder_1_s, halfadder_2_c;

  halfadder halfadder_1 (.A(A), .B(B), .S(halfadder_1_s), .C(halfadder_1_c));
  halfadder halfadder_2 (.A(CI), .B(halfadder_1_s), .S(S), .C(halfadder_2_c));
  or or_1 (CO, halfadder_2_c, halfadder_1_c);
endmodule
