// Digital circuit instruction_memory.dig as structural Verilog
module instruction_memory (
  input  [7:0] addr,
  input  [1:0] Nd,
  output [31:0] D
);

  wire [31:0] fib_rec_s_d, getbit_seq_s_d, is_pal_rec_s_d, quadratic_s_d;

  ROM #(.AddrBits(8), .Bits(32)) fib_rec_s (.A(addr), .sel(1'b1), .D(fib_rec_s_d));
  ROM #(.AddrBits(8), .Bits(32)) getbit_seq_s (.A(addr), .sel(1'b1), .D(getbit_seq_s_d));
  ROM #(.AddrBits(8), .Bits(32)) is_pal_rec_s (.A(addr), .sel(1'b1), .D(is_pal_rec_s_d));
  ROM #(.AddrBits(8), .Bits(32)) quadratic_s (.A(addr), .sel(1'b1), .D(quadratic_s_d));
  Multiplexer #(.Selector_Bits(2), .Bits(32)) multiplexer_1 (
    .sel(Nd), .in_0(fib_rec_s_d), .in_1(is_pal_rec_s_d), .in_2(getbit_seq_s_d), .in_3(quadratic_s_d), .out(D));

  // Notes on the sheet:
  //   contents of fib_rec_s (hex, n*v repeats v):
  //   e24dd008,e58de000,e3500001,da000009,e2400001,e58d0004,ebfffffe
  //   ,e1a01000,e59d0004,e2400001,e58d1004,ebfffffe,e59d1004,e0800001
  //   ,e59de000,e28dd008,e12fff1e,e2800000
  //   contents of getbit_seq_s (hex, n*v repeats v):
  //   e042c001,e1a00130,e3a03001,e1a03f83,e1a03c53,e26cc01f,e1a03c33
  //   ,e0000003,e12fff1e,e2800000
  //   contents of is_pal_rec_s (hex, n*v repeats v):
  //   e24dd008,e58de000,e1510002,aa000007,e7d03001,e7d0c002,e153000c
  //   ,1a000005,e2811001,e2422001,ebfffffe,ea000002,e3a00001,ea000000
  //   ,e3a00000,e59de000,e28dd008,e12fff1e,e2800000
  //   contents of quadratic_s (hex, n*v repeats v):
  //   e0020290,e0000090,e0000091,e0820000,e0830000,e12fff1e,e2800000
endmodule
