// Digital circuit project05.dig as structural Verilog
module project05 (
  input  [1:0] PROG,
  input  CLR,
  input  CLK,
  output DONE,
  output [7:0] TOTAL,
  output [7:0] MUL,
  output [7:0] BX,
  output [7:0] BL,
  output [7:0] BCC,
  output [7:0] B,
  output [7:0] MEM,
  output [7:0] DP
);

  wire and_1_out, decoder_1_out_1, decoder_1_out_2, decoder_1_out_3, decoder_1_out_4, decoder_1_out_5,
       decoder_1_out_6, decoder_1_out_7;
  wire [2:0] analyze_decode_1_itype;
  wire [7:0] _8bit_adder_1_sum, multiplexer_1_out;
  wire [31:0] instruction_memory_1_d;

  and and_1 (and_1_out, CLK, ~DONE);  // And
  _8bit_counter _8bit_counter_1 (.CLK(and_1_out), .CLR(CLR), .COUNT(TOTAL));
  instruction_memory instruction_memory_1 (.addr(TOTAL), .Nd(PROG), .D(instruction_memory_1_d));
  _32bit_eq _32bit_eq_1 (.a(instruction_memory_1_d), .b(32'he2800000), .r(DONE));
  analyze_decode analyze_decode_1 (.iw(instruction_memory_1_d), .itype(analyze_decode_1_itype));
  _8bit_adder _8bit_adder_1 (.A(8'h1), .B(multiplexer_1_out), .sum(_8bit_adder_1_sum));
  Decoder #(.Selector_Bits(3)) decoder_1 (
    .sel(analyze_decode_1_itype), .out_1(decoder_1_out_1), .out_2(decoder_1_out_2), .out_3(decoder_1_out_3),
    .out_4(decoder_1_out_4), .out_5(decoder_1_out_5), .out_6(decoder_1_out_6), .out_7(decoder_1_out_7));  // open: out_0
  _8bit_register_cir_en _8bit_register_cir_en_1 (
    .D(_8bit_adder_1_sum), .EN(decoder_1_out_1), .CLR(CLR), .CLK(and_1_out), .Q(DP));
  _8bit_register_cir_en _8bit_register_cir_en_2 (
    .D(_8bit_adder_1_sum), .EN(decoder_1_out_2), .CLR(CLR), .CLK(and_1_out), .Q(MEM));
  _8bit_register_cir_en _8bit_register_cir_en_3 (
    .D(_8bit_adder_1_sum), .EN(decoder_1_out_3), .CLR(CLR), .CLK(and_1_out), .Q(B));
  _8bit_register_cir_en _8bit_register_cir_en_4 (
    .D(_8bit_adder_1_sum), .EN(decoder_1_out_5), .CLR(CLR), .CLK(and_1_out), .Q(BCC));
  _8bit_register_cir_en _8bit_register_cir_en_5 (
    .D(_8bit_adder_1_sum), .EN(decoder_1_out_4), .CLR(CLR), .CLK(and_1_out), .Q(BL));
  _8bit_register_cir_en _8bit_register_cir_en_6 (
    .D(_8bit_adder_1_sum), .EN(decoder_1_out_7), .CLR(CLR), .CLK(and_1_out), .Q(BX));
  _8bit_register_cir_en _8bit_register_cir_en_7 (
    .D(_8bit_adder_1_sum), .EN(decoder_1_out_6), .CLR(CLR), .CLK(and_1_out), .Q(MUL));
  Multiplexer #(.Bits(8), .Selector_Bits(3)) multiplexer_1 (
    .sel(analyze_decode_1_itype), .in_0({8{1'b0}}), .in_1(DP), .in_2(MEM), .in_3(B), .in_4(BL), .in_5(BCC),
    .in_6(MUL), .in_7(BX), .out(multiplexer_1_out));

  // Notes on the sheet:
  //   CLR: default 1
  //   CLK: Hz: 5
endmodule
