// Digital circuit set_reset_latch.dig as structural Verilog
module set_reset_latch (
  input  R,
  input  S,
  output Q,
  output NotQ
);

  nor nor_1 (Q, R, NotQ);
  nor nor_2 (NotQ, Q, S);
endmodule
